# Fritzing sketch Esquematico_ejercicio_2 (saved by Fritzing 1.0.5)
breadboards: 1

parts:
  Componente1 = Arduino Mega 2560 (Rev3)
  R1 = Resistor [tolerance=±5% resistance=10K package="2512 [SMD]"]
  R2 = Resistor [tolerance=±5% power=0.25W resistance=150 package=THT]
  S1 = Pushbutton [package="[THT]"]
  C3 = Ceramic Capacitor [capacitance=100nF voltage=35V package="1206 [SMD, multilayer]"]
  R3 = Resistor [tolerance=±5% power=0.25W resistance=220 package=THT]
  LED1 = smd LED [color="Red (633nm)" package="0805 [SMD]"]
  R4 = Resistor [tolerance=±5% power=0.25W resistance=150 package=THT]
  S2 = Pushbutton [package="[THT]"]
  R5 = Resistor [tolerance=±5% resistance=10K package="2512 [SMD]"]
  C4 = Ceramic Capacitor [capacitance=100nF voltage=35V package="1206 [SMD, multilayer]"]
  LED2 = smd LED [color="Yellow (585nm)" package="0805 [SMD]"]
  R6 = Resistor [tolerance=±5% power=0.25W resistance=220 package=THT]

nets:
  N1: Componente1.GND, S1.Pin_1, S1.Pin_2, C3.0, R3.Pin_1, S2.Pin_1, S2.Pin_2, C4.0, R6.Pin_1
  N2: Componente1.D10_PWM, LED2.cathode
  N3: Componente1.D9_PWM, LED1.cathode
  N4: Componente1.5V, R2.Pin_0, R4.Pin_0
  N5: Componente1.D2_PWM, R1.Pin_0, C3.1
  N6: Componente1.D3_PWM, R5.Pin_0, C4.1
  N7: R1.Pin_1, R2.Pin_1, S1.Pin_3, S1.Pin_4
  N8: R3.Pin_0, LED1.anode
  N9: R4.Pin_1, S2.Pin_3, S2.Pin_4, R5.Pin_1
  N10: LED2.anode, R6.Pin_0
