# Fritzing sketch esquematico_1 (saved by Fritzing 1.0.5)
breadboards: 1

parts:
  Componente2 = Arduino Mega 2560 (Rev3)
  R3 = Resistor [tolerance=±5% power=0.25W resistance=150 package=THT]
  S2 = Pushbutton [package="[THT]"]

nets:
  N1: Componente2.GND, S2.Pin_1, S2.Pin_2
  N2: Componente2.5V, R3.Pin_0
  N3: Componente2.D2_PWM, R3.Pin_1, S2.Pin_3, S2.Pin_4
