# Fritzing sketch esquematico_funcionalidad_extra (saved by Fritzing 1.0.5)
breadboards: 1

parts:
  Componente1 = Arduino Mega 2560 (Rev3)
  R1 = Resistor [tolerance=±5% resistance=10K package="2512 [SMD]"]
  R2 = Resistor [tolerance=±5% power=0.25W resistance=150 package=THT]
  S1 = Pushbutton [package="[THT]"]
  C3 = Ceramic Capacitor [capacitance=100nF voltage=35V package="1206 [SMD, multilayer]"]
  R3 = Resistor [tolerance=±5% power=0.25W resistance=220 package=THT]
  LED1 = RGB LED (com. anode, rbg) [color="Red (633nm)" current=0.030A package="5 mm [THT]"]
  R4 = Resistor [tolerance=±5% power=0.25W resistance=220 package=THT]
  R5 = Resistor [tolerance=±5% power=0.25W resistance=220 package=THT]

nets:
  N1: Componente1.GND, S1.Pin_1, S1.Pin_2, C3.0
  N2: Componente1.D11_PWM, R5.Pin_0
  N3: Componente1.D10_PWM, R4.Pin_1
  N4: Componente1.D9_PWM, R3.Pin_1
  N5: Componente1.5V, R2.Pin_0, LED1.common_anode
  N6: Componente1.D2_PWM, R1.Pin_0, C3.1
  N7: R1.Pin_1, R2.Pin_1, S1.Pin_3, S1.Pin_4
  N8: R3.Pin_0, LED1.green_cathode
  N9: LED1.red_cathode, R5.Pin_1
  N10: LED1.blue_cathode, R4.Pin_0
