# Fritzing sketch ejercicio_1 (saved by Fritzing 1.0.5)
breadboards: 1

parts:
  Componente1 = Arduino Mega 2560 (Rev3)
  U1 = CNZ1120 [package=cnz1120]
  R1 = Resistor [tolerance=±5% resistance=10k package="1206 [SMD]"]
  R2 = Resistor [tolerance=±5% resistance=330 package="1206 [SMD]"]

nets:
  N1: Componente1.GND, R1.Pin_1, R2.Pin_0
  N2: Componente1.5V, U1.2, U1.4
  N3: Componente1.D3_PWM, U1.3, R1.Pin_0
  N4: U1.1, R2.Pin_1
