# Fritzing sketch funcionalidad_extra (saved by Fritzing 1.0.5)
breadboards: 1

parts:
  Componente1 = Arduino Mega 2560 (Rev3)
  U1 = CNZ1120 [package=cnz1120]
  R1 = Resistor [tolerance=±5% resistance=10k package="1206 [SMD]"]
  R2 = Resistor [tolerance=±5% resistance=330 package="1206 [SMD]"]
  S1 = Pushbutton [package="[SMD]"]
  R3 = Resistor [tolerance=±5% resistance=150 package="1206 [SMD]"]
  R4 = Resistor [tolerance=±5% resistance=100k package="1206 [SMD]"]
  C1 = Capacitor [package=cap-pth-large]

nets:
  N1: Componente1.GND, R1.Pin_1, R2.Pin_0, S1.Pin_1, S1.Pin_2, C1.1
  N2: Componente1.5V, U1.2, U1.4, R4.Pin_0
  N3: Componente1.D2_PWM, R3.Pin_0, C1.2
  N4: Componente1.D3_PWM, U1.3, R1.Pin_0
  N5: U1.1, R2.Pin_1
  N6: S1.Pin_3, S1.Pin_4, R3.Pin_1, R4.Pin_1
