# Fritzing sketch funcionalidad_extra (saved by Fritzing 1.0.5)
breadboards: 1

parts:
  Componente1 = Arduino Mega 2560 (Rev3)
  HC-SR04_Sensor_1 = HC-SR04 Ultrasonic Distance Sensor
  LED1 = smd LED [color="Green (555nm)" package="1206 [SMD]"]
  R1 = Resistor [tolerance=±5% resistance=220 package="0402 [SMD]"]
  LED2 = smd LED [color="Yellow (595nm)" package="1206 [SMD]"]
  R2 = Resistor [tolerance=±5% resistance=220 package="0402 [SMD]"]
  LED3 = smd LED [color="Red (635nm)" package="1206 [SMD]"]
  R3 = Resistor [tolerance=±5% resistance=220 package="0402 [SMD]"]
  J1 = Piezo Speaker

nets:
  GND: Componente1.GND, HC-SR04_Sensor_1.GND, R1.Pin_1, R2.Pin_1, R3.Pin_1, J1.pin1
  5V: Componente1.5V, HC-SR04_Sensor_1.VCC
  N1: Componente1.D2_PWM, J1.pin2
  N2: Componente1.D3_PWM, HC-SR04_Sensor_1.TRIG
  N3: Componente1.D4_PWM, HC-SR04_Sensor_1.ECHO
  N4: Componente1.D5_PWM, LED1.cathode
  N5: Componente1.D6_PWM, LED2.cathode
  N6: Componente1.D7_PWM, LED3.cathode
  N7: LED1.anode, R1.Pin_0
  N8: LED2.anode, R2.Pin_0
  N9: LED3.anode, R3.Pin_0
