# Fritzing sketch esquematico_ejercicio (saved by Fritzing 1.0.1rc)
breadboards: 1

parts:
  Componente2 = Arduino Mega 2560 (Rev3)
  S1 = Reed switch [package=THT]
  R1 = Resistor [tolerance=±5% resistance=10k package="2512 [SMD]"]
  R2 = Resistor [tolerance=±5% resistance=220 package="2512 [SMD]"]
  LED1 = smd LED [color="Red (633nm)" package="0805 [SMD]"]

nets:
  N1: Componente2.5V, R1.Pin_0
  N2: Componente2.GND, S1.pin_1, LED1.anode
  N3: Componente2.D2_PWM, S1.pin_2, R1.Pin_1
  N4: Componente2.D3_PWM, R2.Pin_0
  N5: R2.Pin_1, LED1.cathode
