# Fritzing sketch ejercicio-2 (saved by Fritzing 1.0.5)
breadboards: 1

parts:
  부품1 = FC-28 Soil Hygrometer Module - Probe
  부품2 = FC-28 Soil Hygrometer Module
  Componente1 = Arduino Mega ADK (Rev3)
  LED1 = smd LED [color="Red (633nm)" package="1206 [SMD]"]
  LED2 = smd LED [color="Green (560nm)" package="1206 [SMD]"]
  LED3 = smd LED [color="Red (633nm)" package="1206 [SMD]"]
  R1 = Resistor [tolerance=±5% resistance=220 package="2512 [SMD]"]
  R2 = Resistor [tolerance=±5% resistance=220 package="2512 [SMD]"]
  R3 = Resistor [tolerance=±5% resistance=220 package="2512 [SMD]"]

nets:
  N1: 부품1.POS, 부품2.POS
  N2: 부품1.NEG, 부품2.NEG
  VCC: 부품2.VCC, Componente1.5V
  GND: 부품2.GND, Componente1.GND, R1.Pin_1, R2.Pin_1, R3.Pin_1
  N3: 부품2.AO, Componente1.A0
  N4: Componente1.D11_PWM, LED3.cathode
  N5: Componente1.D10_PWM, LED2.cathode
  N6: Componente1.D9_PWM, LED1.cathode
  N7: LED1.anode, R1.Pin_0
  N8: LED2.anode, R2.Pin_0
  N9: LED3.anode, R3.Pin_0

custom parts:
  FC-28 Soil Hygrometer Module - Probe: The FC-28 is a soil hygrometer module that uses the Texas Instruments LM393 comparator chip to provide an analog measurement of soil humidity.
  FC-28 Soil Hygrometer Module: The FC-28 is a soil hygrometer module that uses the Texas Instruments LM393 comparator chip to provide an analog measurement of soil humidity. The digital output is high when soil moisture is over a certain threshold, as determined by adjusting the potentiometer.
