# Fritzing sketch ejercicio (saved by Fritzing 1.0.5)
breadboards: 1

parts:
  Componente1 = HC-SR501 Body Sensor Module
  Componente3 = Arduino Mega 2560 (Rev3)
  J1 = Basic Force Sensing Resistor (FSR) [package=THT]
  LED1 = LED - 5mm [color="Green (555nm)" current=0.030A package="5 mm [THT]"]
  R1 = Resistor [tolerance=±5% power=0.25W resistance=220 package=THT]
  R2 = Resistor [tolerance=±5% power=0.25W resistance=10k package=THT]

nets:
  VCC: Componente1.VCC, Componente3.5V, J1.pin_0
  N1: Componente1.OUT, Componente3.D2_PWM
  GND: Componente1.GND, Componente3.GND, R1.Pin_1, R2.Pin_1
  N2: Componente3.A0, J1.pin_1, R2.Pin_0
  N3: Componente3.D3_PWM, LED1.cathode
  N4: LED1.anode, R1.Pin_0

custom parts:
  HC-SR501 Body Sensor Module: Pyroelectric Infrared PIR Motion Sensor Detector Module
