# Fritzing sketch esquematico_ejercicio_1_2 (saved by Fritzing 1.0.5)

parts:
  Componente3 = Arduino Mega 2560 (Rev3)
  J1 = Basic Servo

nets:
  GND: Componente3.GND, J1.gnd
  N1: Componente3.D9_PWM, J1.pulse
  5V: Componente3.5V, J1.vcc
